# Fritzing sketch sinkku (saved by Fritzing 0.9.0b)
breadboards: 1

parts:
  AD1 = DDS AD9850
  Bauteil1 = Arduino Leonardo (Rev3b)
  Nokia_5110_LCD_Module1 = Nokia5110LCDModule

nets:
  VCC: AD1.VCC, Bauteil1.5V
  GND: AD1.GND, Bauteil1.GND, Nokia_5110_LCD_Module1.Grnd
  N1: AD1.CLK, Bauteil1.D8/A8
  N2: AD1.FQ, Bauteil1.D9_PWM/A9
  N3: AD1.DATA, Bauteil1.D10_PWM/A10
  N4: AD1.RST, Bauteil1.D11_PWM
  N5: Bauteil1.D2/SDA, Bauteil1.SDA, Nokia_5110_LCD_Module1.RST
  N6: Bauteil1.D3_PWM/SCL, Bauteil1.SCL, Nokia_5110_LCD_Module1.SCLK
  N7: Bauteil1.D4/A6, Nokia_5110_LCD_Module1.SCE
  N8: Bauteil1.D5_PWM, Nokia_5110_LCD_Module1.6_DN_(MOSI)
  N9: Bauteil1.D6_PWM/A7, Nokia_5110_LCD_Module1.D/C
  3V3: Bauteil1.3V3, Nokia_5110_LCD_Module1.Vcc

custom parts:
  DDS AD9850: AD9850 DDS Signal Generator Module, frequency range 0 to 40MHz, sine or square wave output, on board 70MHz low pass filter, and 125MHz clock module. https://code.google.com/p/ad9850-arduino/
  : Nokia 5110 LCD with 8 pin. It's a 45mm*45mm module part. Description: The Nokia 5110 is a basic graphic LCD screen for lots of applications. It was originally intended for as a cell phone screen. This one is mounted on an easy to solder PCB. It uses the PCD8544 controller. The PCD8544 is a low power CMOS LCD controller/driver, designed to drive a graphic display of 48 rows and 84 columns. All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
